# Fritzing sketch Uno_radioFeatherwing (saved by Fritzing 0.9.3b)

parts:
  Composant7 = Arduino Uno (Rev3)
  Composant6 = Adafruit Radio FeatherWing [part_number="Adafruit #3229, 3230, 3231, 3232"]
  U1 = ESP8266 WiFi Module [part_number=ESP8266]

nets:
  N1: Composant7.D9_PWM, Composant6.RF_RST, Composant6.B
  N2: Composant7.D10_PWM/SS, Composant6.CS, Composant6.C
  N3: Composant7.D11_PWM/MOSI, Composant6.MOSI
  N4: Composant7.D12/MISO, Composant6.MISO
  N5: Composant7.D13/SCK, Composant6.SCK
  N6: Composant7.D2, Composant6.IRQ, Composant6.A
  N7: Composant7.D5_PWM, U1.GPIO_2
  N8: Composant7.D6_PWM, U1.GPIO_0
  3V3: Composant7.3V3, Composant6.3.3V, U1.VCC, U1.CH_PD
  GND: Composant7.GND, Composant6.GND, U1.GND

custom parts:
  Adafruit Radio FeatherWing: Add short-hop wireless to your Feather with these Radio Featherwings. These add-ons for any Feather board will let you integrate packetized radio (with the RFM69 radio) or LoRa radio (with the RFM9x's). These radios are good options for kilometer-range radio, and paired with one of our WiFi, cellular or Bluetooth Feathers, will let you bridge from 433/900 MHz to the Internet or your mobile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
  ESP8266 WiFi Module: Generic WiFi Module based on the ESP8266 with onboard PCB antenna and UART communications
